// Logisim project lab6rotr.circ as structural Verilog
module shift_by_1 (
  input  [15:0] in_1,
  input  in_2,
  output [15:0] out_3
);

  Multiplexer #(.width(16)) multiplexer_1 (
    .in0(in_1), .in1({in_1[0], in_1[15:1]}), .out(out_3), .sel(in_2));  // open: en
endmodule

module shift_by_2 (
  input  [15:0] in_1,
  input  in_2,
  output [15:0] out_3
);

  Multiplexer #(.width(16)) multiplexer_1 (
    .in0(in_1), .in1({in_1[1:0], in_1[15:2]}), .out(out_3), .sel(in_2));  // open: en
endmodule

module shift_by_4 (
  input  [15:0] in_1,
  input  in_2,
  output [15:0] out_3
);

  Multiplexer #(.width(16)) multiplexer_1 (
    .in0(in_1), .in1({in_1[3:0], in_1[15:4]}), .out(out_3), .sel(in_2));  // open: en
endmodule

module shift_by_8 (
  input  [15:0] in_1,
  input  in_2,
  output [15:0] out_3
);

  Multiplexer #(.width(16)) multiplexer_1 (
    .in0(in_1), .in1({in_1[7:0], in_1[15:8]}), .out(out_3), .sel(in_2));  // open: en
endmodule

module rotr (
  input  [15:0] in_1,
  input  [3:0] in_2,
  output [15:0] out_3
);

  wire [15:0] shift_by_1_1_out_3, shift_by_2_1_out_3, shift_by_4_1_out_3;

  shift_by_1 shift_by_1_1 (.in_1(in_1), .in_2(in_2[0]), .out_3(shift_by_1_1_out_3));
  shift_by_2 shift_by_2_1 (.in_1(shift_by_1_1_out_3), .in_2(in_2[1]), .out_3(shift_by_2_1_out_3));
  shift_by_4 shift_by_4_1 (.in_1(shift_by_2_1_out_3), .in_2(in_2[2]), .out_3(shift_by_4_1_out_3));
  shift_by_8 shift_by_8_1 (.in_1(shift_by_4_1_out_3), .in_2(in_2[3]), .out_3(out_3));
endmodule
