// Logisim project lab6splitters.circ as structural Verilog: 2 circuits, main circuit main
module main (
  input  [7:0] firstPin,
  output Out1,
  output [7:0] out_3
);

  not not_1 (out_3[7], firstPin[7]);
  and and_1 (Out1, firstPin[0], firstPin[7]);

  assign out_3[6:0] = firstPin[6:0];
endmodule

module Ex1 (
  input  [7:0] firstPin,
  output Out1,
  output [7:0] Out2,
  output [7:0] Out2_2
);

  wire [7:0] adder_1_out, not_1_out, or_1_out;

  and and_1 (Out1, firstPin[0], firstPin[7]);
  assign not_1_out = ~firstPin;  // NOT_Gate not_1, 8 bits wide
  Adder adder_1 (.a(not_1_out), .b(8'h1), .out(adder_1_out));  // open: cin, cout
  assign or_1_out = 8'h80 | adder_1_out;  // OR_Gate or_1, 8 bits wide
  Multiplexer #(.width(8)) multiplexer_1 (.in0(firstPin), .in1(or_1_out), .out(Out2), .sel(firstPin[7]));  // open: en
endmodule
